# Fritzing sketch chytra-budka (saved by Fritzing 1.0.0)

parts:
  XIAO = XIAO ESP32S3(SENCE)
  MAX17048 = MAX1704X [package=tdfn-8]
  SHT41 = Triple Axis Magnetometer - HMC5883 Breakout
  PIR = PIR sensor
  TP4056 = USB LiPoly Charger
  BATT = LIPO-2000mAh [package=lipo-2000]
  SOLAR = Small 6V Solar Panel
  IRDRV = Humidity Sensor - HIH-4030 Breakout

nets:
  N1: XIAO.D2, PIR.SIG
  N2: XIAO.D3, IRDRV.OUT
  N3: XIAO.D4, MAX17048.SDA, SHT41.SDA
  N4: XIAO.D5, MAX17048.SCL, SHT41.SCL
  3V3: XIAO.3V3, MAX17048.VDD, SHT41.VCC
  GND: XIAO.GND, MAX17048.GND, SHT41.GND, PIR.GND, TP4056.GND, BATT.-, SOLAR.-, IRDRV.GND
  5V: XIAO.5V, MAX17048.CELL, PIR.VDD, TP4056.VBAT, BATT.+, SOLAR.+, IRDRV.VCC

custom parts:
  XIAO ESP32S3(SENCE): Seeed Studio XIAO ESP32S3 leverages dual-core ESP32S3 chip, supporting both Wi-Fi and BLE wireless connectivities, which allows battery charge. It integrates built-in camera sensor, digital microphone. It offers 8MB PSRAM, 8MB FLASH, and external SD card slot. All of these make it suitable for embedded ML, like intelligent voice and vision AI.
